// Logisim project ANMD_TV-tennis.circ as structural Verilog: 11 circuits, main circuit sr
module sr (
  input  [4:0] in_1,
  input  [4:0] in_2,
  output out_3
);

  wire [4:0] xnor_1_out;

  assign xnor_1_out = ~(in_1 ^ in_2);  // XNOR_Gate xnor_1, 5 bits wide
  and and_1 (out_3, xnor_1_out[0], xnor_1_out[1], xnor_1_out[2], xnor_1_out[3], xnor_1_out[4]);
endmodule

module screen (
);

  wire button_1_out, button_2_out, hard_mode_out_3, reset_out;
  wire [1:0] joystick_1_y;
  wire [3:0] sc_1_out_2, sc_1_out_3, sc_2_out_2, sc_2_out_3;
  wire [4:0] con_1_ballx, con_1_bally, con_1_leftyout, con_1_rightyout, con_1_zero, rob_1_out_5,
       video8_1_ballx_2, video8_1_bally_2, video8_1_chipid_2, video8_1_leftbaty_2, video8_1_rightbaty_2,
       video8_2_ballx_2, video8_2_bally_2, video8_2_chipid_2, video8_2_leftbaty_2, video8_2_rightbaty_2,
       video8_3_ballx_2, video8_3_bally_2, video8_3_chipid_2, video8_3_leftbaty_2, video8_3_rightbaty_2;
  wire [7:0] con_1_scorea, con_1_scoreb, con_1_vxy, con_1_xball, con_1_yball, hard_mode_out_4;
  wire [31:0] video8_1_ot1, video8_1_ot2, video8_1_ot3, video8_1_ot4, video8_1_ot5, video8_1_ot6,
       video8_1_ot7, video8_1_ot8, video8_2_ot1, video8_2_ot2, video8_2_ot3, video8_2_ot4, video8_2_ot5,
       video8_2_ot6, video8_2_ot7, video8_2_ot8, video8_3_ot1, video8_3_ot2, video8_3_ot3, video8_3_ot4,
       video8_3_ot5, video8_3_ot6, video8_3_ot7, video8_3_ot8, video8_4_ot1, video8_4_ot2, video8_4_ot3,
       video8_4_ot4, video8_4_ot5, video8_4_ot6, video8_4_ot7, video8_4_ot8;

  Button button_1 (.out(button_1_out));
  Button button_2 (.out(button_2_out));
  Joystick #(.bits(2)) joystick_1 (.y(joystick_1_y));  // open: x
  LED led_1 (.in(hard_mode_out_3));
  lvl hard_mode (.in_1(button_1_out), .in_2(button_2_out), .out_3(hard_mode_out_3), .out_4(hard_mode_out_4));
  DotMatrix #(.matrixcols(32), .matrixrows(32)) dotmatrix_1 (
    .col0(video8_1_ot1), .col1(video8_1_ot2), .col2(video8_1_ot3), .col3(video8_1_ot4), .col4(video8_1_ot5),
    .col5(video8_1_ot6), .col6(video8_1_ot7), .col7(video8_1_ot8), .col8(video8_2_ot1), .col9(video8_2_ot2),
    .col10(video8_2_ot3), .col11(video8_2_ot4), .col12(video8_2_ot5), .col13(video8_2_ot6),
    .col14(video8_2_ot7), .col15(video8_2_ot8), .col16(video8_3_ot1), .col17(video8_3_ot2),
    .col18(video8_3_ot3), .col19(video8_3_ot4), .col20(video8_3_ot5), .col21(video8_3_ot6),
    .col22(video8_3_ot7), .col23(video8_3_ot8), .col24(video8_4_ot1), .col25(video8_4_ot2),
    .col26(video8_4_ot3), .col27(video8_4_ot4), .col28(video8_4_ot5), .col29(video8_4_ot6),
    .col30(video8_4_ot7), .col31(video8_4_ot8));
  Button reset (.out(reset_out));
  con con_1 (
    .rightYin(rob_1_out_5), .vxy(con_1_vxy), .xball(con_1_xball), .yball(con_1_yball), .reset(reset_out),
    .leftYin(joystick_1_y), .scoreA(con_1_scorea), .scoreB(con_1_scoreb), .ballX(con_1_ballx),
    .ballY(con_1_bally), .leftYout(con_1_leftyout), .rightYout(con_1_rightyout), .zero(con_1_zero));
  rob rob_1 (.out_5(rob_1_out_5), .vxy(con_1_vxy), .xball(con_1_xball), .yball(con_1_yball), .lvl(hard_mode_out_4));
  video8 video8_1 (
    .ballX(con_1_ballx), .ballY(con_1_bally), .leftbatY(con_1_leftyout), .rightbatY(con_1_rightyout),
    .chipID(con_1_zero), .ballX_2(video8_1_ballx_2), .ballY_2(video8_1_bally_2),
    .leftbatY_2(video8_1_leftbaty_2), .rightbatY_2(video8_1_rightbaty_2), .chipID_2(video8_1_chipid_2),
    .ot1(video8_1_ot1), .ot2(video8_1_ot2), .ot3(video8_1_ot3), .ot4(video8_1_ot4), .ot5(video8_1_ot5),
    .ot6(video8_1_ot6), .ot7(video8_1_ot7), .ot8(video8_1_ot8));
  sc sc_1 (.in_1(con_1_scoreb), .out_2(sc_1_out_2), .out_3(sc_1_out_3));
  sc sc_2 (.in_1(con_1_scorea), .out_2(sc_2_out_2), .out_3(sc_2_out_3));
  Hex_Digit_Display hex_digit_display_1 (.value(sc_2_out_2));  // open: dp
  video8 video8_2 (
    .ballX(video8_1_ballx_2), .ballY(video8_1_bally_2), .leftbatY(video8_1_leftbaty_2),
    .rightbatY(video8_1_rightbaty_2), .chipID(video8_1_chipid_2), .ballX_2(video8_2_ballx_2),
    .ballY_2(video8_2_bally_2), .leftbatY_2(video8_2_leftbaty_2), .rightbatY_2(video8_2_rightbaty_2),
    .chipID_2(video8_2_chipid_2), .ot1(video8_2_ot1), .ot2(video8_2_ot2), .ot3(video8_2_ot3),
    .ot4(video8_2_ot4), .ot5(video8_2_ot5), .ot6(video8_2_ot6), .ot7(video8_2_ot7), .ot8(video8_2_ot8));
  Hex_Digit_Display hex_digit_display_2 (.value(sc_2_out_3));  // open: dp
  video8 video8_3 (
    .ballX(video8_2_ballx_2), .ballY(video8_2_bally_2), .leftbatY(video8_2_leftbaty_2),
    .rightbatY(video8_2_rightbaty_2), .chipID(video8_2_chipid_2), .ballX_2(video8_3_ballx_2),
    .ballY_2(video8_3_bally_2), .leftbatY_2(video8_3_leftbaty_2), .rightbatY_2(video8_3_rightbaty_2),
    .chipID_2(video8_3_chipid_2), .ot1(video8_3_ot1), .ot2(video8_3_ot2), .ot3(video8_3_ot3),
    .ot4(video8_3_ot4), .ot5(video8_3_ot5), .ot6(video8_3_ot6), .ot7(video8_3_ot7), .ot8(video8_3_ot8));
  Hex_Digit_Display hex_digit_display_3 (.value(sc_1_out_2));  // open: dp
  video8 video8_4 (
    .ballX(video8_3_ballx_2), .ballY(video8_3_bally_2), .leftbatY(video8_3_leftbaty_2),
    .rightbatY(video8_3_rightbaty_2), .chipID(video8_3_chipid_2), .ot1(video8_4_ot1), .ot2(video8_4_ot2),
    .ot3(video8_4_ot3), .ot4(video8_4_ot4), .ot5(video8_4_ot5), .ot6(video8_4_ot6), .ot7(video8_4_ot7),
    .ot8(video8_4_ot8));  // open: ballX_2, ballY_2, leftbatY_2, rightbatY_2, chipID_2
  Hex_Digit_Display hex_digit_display_4 (.value(sc_1_out_3));  // open: dp

  // Notes on the sheet:
  //   Professional
  //   Enjoyer
endmodule

module video (
  input  [4:0] ballX,
  input  [4:0] ballY,
  input  [4:0] leftbatY,
  input  [4:0] rightbatY,
  input  [4:0] chipID,
  output [4:0] ballX_2,
  output [4:0] ballY_2,
  output [4:0] leftbatY_2,
  output [4:0] rightbatY_2,
  output [4:0] chipID_2,
  output [31:0] ot
);

  wire sr_1_out_3, sr_2_out_3, sr_3_out_3;
  wire [2:0] multiplexer_1_out, multiplexer_2_out;
  wire [31:0] bit_extender_1_out, bit_extender_2_out, bit_extender_3_out, shifter_1_out, shifter_2_out,
       shifter_3_out;

  Adder #(.width(5)) adder_1 (.a(chipID), .b(5'b00001), .out(chipID_2));  // open: cin, cout
  sr sr_1 (.in_1(ballX), .in_2(chipID), .out_3(sr_1_out_3));
  sr sr_2 (.in_1(chipID), .in_2(5'b00011), .out_3(sr_2_out_3));
  sr sr_3 (.in_1(chipID), .in_2(5'b11100), .out_3(sr_3_out_3));
  assign bit_extender_1_out = {{31{1'b0}}, sr_1_out_3};  // Bit_Extender bit_extender_1
  Multiplexer #(.width(3)) multiplexer_1 (
    .in0(3'b000), .in1(3'b111), .out(multiplexer_1_out), .sel(sr_2_out_3));  // open: en
  Multiplexer #(.width(3)) multiplexer_2 (
    .in0(3'b000), .in1(3'b111), .out(multiplexer_2_out), .sel(sr_3_out_3));  // open: en
  Shifter #(.width(32)) shifter_1 (.in(bit_extender_1_out), .\dist (ballY), .out(shifter_1_out));
  assign bit_extender_2_out = {{29{1'b0}}, multiplexer_1_out};  // Bit_Extender bit_extender_2
  assign bit_extender_3_out = {{29{1'b0}}, multiplexer_2_out};  // Bit_Extender bit_extender_3
  Shifter #(.width(32)) shifter_2 (.in(bit_extender_2_out), .\dist (leftbatY), .out(shifter_2_out));
  Shifter #(.width(32)) shifter_3 (.in(bit_extender_3_out), .\dist (rightbatY), .out(shifter_3_out));
  assign ot = shifter_1_out | shifter_2_out | shifter_3_out;  // OR_Gate or_1, 32 bits wide

  assign ballX_2 = ballX;
  assign ballY_2 = ballY;
  assign leftbatY_2 = leftbatY;
  assign rightbatY_2 = rightbatY;

  // Other names for the same wires on the sheet: a[4:0] = ballY; b[4:0] = leftbatY; c[4:0] = rightbatY;
  //   ID[4:0] = chipID
endmodule

module reflect (
  input  [2:0] in_1,
  output [2:0] out_2
);

  wire a;
  wire [2:0] negator_1_out, not_1_out;

  Comparator #(.width(3)) comparator_1 (.a(in_1), .b(3'b100), .eq(a));  // open: gt, lt
  Negator #(.width(3)) negator_1 (.in(in_1), .out(negator_1_out));
  assign not_1_out = ~in_1;  // NOT_Gate not_1, 3 bits wide
  Multiplexer #(.width(3)) multiplexer_1 (.in0(negator_1_out), .in1(not_1_out), .out(out_2), .sel(a));  // open: en
endmodule

module inrange (
  input  [4:0] in_1,
  input  [4:0] in_2,
  output bus_0
);

  wire comparator_1_eq, comparator_2_eq, comparator_3_eq;
  wire [4:0] adder_1_out, adder_2_out;

  Adder #(.width(5)) adder_1 (.a(in_1), .b(5'b00001), .out(adder_1_out));  // open: cin, cout
  Adder #(.width(5)) adder_2 (.a(in_1), .b(5'b00010), .out(adder_2_out));  // open: cin, cout
  Comparator #(.width(5)) comparator_1 (.a(in_1), .b(in_2), .eq(comparator_1_eq));  // open: gt, lt
  Comparator #(.width(5)) comparator_2 (.a(adder_2_out), .b(in_2), .eq(comparator_2_eq));  // open: gt, lt
  Comparator #(.width(5)) comparator_3 (.a(adder_1_out), .b(in_2), .eq(comparator_3_eq));  // open: gt, lt
  or or_1 (bus_0, comparator_3_eq, comparator_2_eq, comparator_1_eq);
endmodule

// Controller
module con (
  input  reset,
  input  [1:0] leftYin,
  input  [4:0] rightYin,
  output [4:0] ballX,
  output [4:0] ballY,
  output [7:0] vxy,
  output [7:0] xball,
  output [7:0] yball,
  output [4:0] leftYout,
  output [4:0] rightYout,
  output [4:0] zero,
  output [7:0] scoreA,
  output [7:0] scoreB
);

  wire adder_3_cout, adder_4_cout, adder_11_cout, adder_12_cout, and_1_out, and_6_out, and_7_out, Bcontact,
       comparator_1_eq, comparator_1_lt, comparator_2_eq, comparator_3_eq, comparator_4_eq, comparator_5_eq,
       comparator_6_eq, comparator_7_eq, comparator_8_eq, hitA, hitB, inrange_1_bus_0, inrange_2_bus_0,
       LBcontact, not_1_out, not_2_out, not_3_out, not_4_out, not_6_out, not_7_out, or_1_out, or_3_out,
       or_4_out, or_5_out, or_6_out, or_7_out, or_8_out, or_10_out, or_11_out, or_12_out, or_13_out,
       random_3_out, RBcontact, reset_t, takt, vxneg, vyneg, xor_3_out, xor_4_out, xrefl, yrefl;
  wire [1:0] adder_2_out, multiplexer_7_out, random_2_out, VleftBat, VrightBat;
  wire [2:0] adder_13_out, adder_14_out, adder_15_out, adder_16_out, adder_17_out, bit_extender_11_out,
       multiplexer_9_out, multiplexer_10_out, multiplexer_11_out, multiplexer_12_out, multiplexer_13_out,
       not_5_out, random_1_out, reflect_1_out_2, reflect_2_out_2, vx, vy, xx, yy;
  wire [4:0] bit_extender_7_out, bit_extender_10_out, gg, leftYin_t, multiplexer_5_out, multiplexer_6_out,
       rightYin_t;
  wire [7:0] adder_1_out, adder_6_out, adder_7_out, adder_8_out, adder_9_out, adder_10_out,
       bit_extender_3_out, bit_extender_4_out, longVX, longVY, multiplexer_1_out, multiplexer_2_out,
       multiplexer_3_out, multiplexer_4_out, shifter_1_out, shifter_2_out, shifter_3_out, shifter_4_out,
       shifter_5_out;

  mcon mcon_1 (.Vy({5{1'b1}}), .Y(rightYin), .bus_0(rightYin_t));
  Shifter #(.shift("lr")) shifter_1 (.in(longVX), .\dist (3'b111), .out(shifter_1_out));
  Shifter #(.shift("lr")) shifter_2 (.in(longVY), .\dist (3'b111), .out(shifter_2_out));
  or or_1 (or_1_out, reset, hitA);
  or or_2 (reset_t, reset, hitB, hitA);
  or or_3 (or_3_out, yrefl, reset_t);
  or or_4 (or_4_out, xrefl, Bcontact, reset_t);
  Bit_Extender #(.out_width(1)) bit_extender_1 (.in(shifter_1_out), .out(vxneg));
  Bit_Extender #(.out_width(1)) bit_extender_2 (.in(shifter_2_out), .out(vyneg));
  Multiplexer #(.width(8)) multiplexer_1 (
    .in0(adder_1_out), .in1({8{1'b0}}), .out(multiplexer_1_out), .sel(reset));  // open: en
  Register scA (.D(multiplexer_1_out), .en(or_1_out), .Q(scoreA), .clk(takt));  // open: clr
  Register #(.width(3)) u_vy (.D(yy), .en(or_3_out), .Q(vy), .clk(takt));  // open: clr
  Register #(.width(3)) u_vx (.D(xx), .en(or_4_out), .Q(vx), .clk(takt));  // open: clr
  Adder adder_1 (.a(scoreA), .b(8'h1), .out(adder_1_out));  // open: cin, cout
  or or_5 (or_5_out, reset, hitB);
  Adder #(.width(2)) adder_2 (.a(2'b10), .b(leftYin), .out(adder_2_out));  // open: cin, cout
  assign bit_extender_3_out = {{5{1'b0}}, vy};  // Bit_Extender bit_extender_3
  assign bit_extender_4_out = {{5{1'b0}}, vx};  // Bit_Extender bit_extender_4
  assign longVY = {{5{vy[2]}}, vy};  // Bit_Extender bit_extender_5
  assign longVX = {{5{vx[2]}}, vx};  // Bit_Extender bit_extender_6
  Adder adder_3 (.a(xball), .b(longVX), .cout(adder_3_cout));  // open: out, cin
  Adder adder_4 (.a(yball), .b(longVY), .cout(adder_4_cout));  // open: out, cin
  Multiplexer #(.width(8)) multiplexer_2 (
    .in0(adder_6_out), .in1({8{1'b0}}), .out(multiplexer_2_out), .sel(reset));  // open: en
  Register scB (.D(multiplexer_2_out), .en(or_5_out), .Q(scoreB), .clk(takt));  // open: clr
  assign bit_extender_7_out = {{3{VleftBat[1]}}, VleftBat};  // Bit_Extender bit_extender_7
  Negator #(.width(2)) negator_1 (.in(adder_2_out), .out(VleftBat));
  not not_1 (not_1_out, Bcontact);
  not not_2 (not_2_out, xrefl);
  Shifter shifter_3 (.in(bit_extender_3_out), .\dist (3'b011), .out(shifter_3_out));
  Adder adder_5 (.a(shifter_3_out), .b(bit_extender_4_out), .out(vxy));  // open: cin, cout
  Clock #(.highDuration(8), .lowDuration(8)) clock_1 (.out(takt));
  xor xor_1 (xrefl, adder_3_cout, vxneg);
  xor xor_2 (yrefl, adder_4_cout, vyneg);
  Adder adder_6 (.a(scoreB), .b(8'h1), .out(adder_6_out));  // open: cin, cout
  mcon mcon_2 (.Vy(bit_extender_7_out), .Y(leftYout), .bus_0(leftYin_t));
  and and_1 (and_1_out, not_1_out, not_2_out);
  not not_3 (not_3_out, vxneg);
  and and_2 (hitB, vxneg, xrefl);
  Adder adder_7 (.a(xball), .b(longVX), .out(adder_7_out));  // open: cin, cout
  Multiplexer #(.width(8)) multiplexer_3 (
    .in0(adder_7_out), .in1(8'h80), .out(multiplexer_3_out), .sel(reset_t));  // open: en
  or or_6 (or_6_out, and_1_out, reset_t);
  Adder adder_8 (.a(yball), .b(longVY), .out(adder_8_out));  // open: cin, cout
  Multiplexer #(.width(8)) multiplexer_4 (
    .in0(adder_8_out), .in1(8'h80), .out(multiplexer_4_out), .sel(reset_t));  // open: en
  not not_4 (not_4_out, yrefl);
  and and_3 (hitA, xrefl, not_3_out);
  Register xreg (.D(multiplexer_3_out), .en(or_6_out), .Q(xball), .clk(takt));  // open: clr
  Register yreg (.D(multiplexer_4_out), .en(or_7_out), .Q(yball), .clk(takt));  // open: clr
  or or_7 (or_7_out, not_4_out, reset_t);
  Adder adder_9 (.a(xball), .b(8'he4), .out(adder_9_out));  // open: cin, cout
  Adder adder_10 (.a(xball), .b(8'h1c), .out(adder_10_out));  // open: cin, cout
  Shifter #(.shift("lr")) shifter_4 (.in(xball), .\dist (3'b011), .out(shifter_4_out));
  Shifter #(.shift("lr")) shifter_5 (.in(yball), .\dist (3'b011), .out(shifter_5_out));
  Multiplexer #(.width(5)) multiplexer_5 (
    .in0(gg), .in1(5'b01111), .out(multiplexer_5_out), .sel(reset_t));  // open: en
  Comparator #(.width(5), .mode("unsigned")) comparator_1 (
    .a(rightYin_t), .b(rightYout), .eq(comparator_1_eq), .lt(comparator_1_lt));  // open: gt
  Adder adder_11 (.a(adder_9_out), .b(longVX), .cout(adder_11_cout));  // open: out, cin
  Adder adder_12 (.a(adder_10_out), .b(longVX), .cout(adder_12_cout));  // open: out, cin
  Bit_Extender #(.out_width(5)) bit_extender_8 (.in(shifter_4_out), .out(ballX));
  Bit_Extender #(.out_width(5)) bit_extender_9 (.in(shifter_5_out), .out(ballY));
  Register #(.width(5)) rightYreg (.D(multiplexer_5_out), .en(1'b1), .Q(rightYout), .clk(takt));  // open: clr
  Multiplexer #(.width(5)) multiplexer_6 (
    .in0(leftYin_t), .in1(5'b01111), .out(multiplexer_6_out), .sel(reset_t));  // open: en
  Multiplexer #(.width(2)) multiplexer_7 (
    .in0(2'b11), .in1(2'b00), .out(multiplexer_7_out), .sel(comparator_1_eq));  // open: en
  xor xor_3 (xor_3_out, adder_11_cout, vxneg);
  inrange inrange_1 (.in_1(leftYin_t), .in_2(ballY), .bus_0(inrange_1_bus_0));
  xor xor_4 (xor_4_out, adder_12_cout, vxneg);
  inrange inrange_2 (.in_1(rightYin_t), .in_2(ballY), .bus_0(inrange_2_bus_0));
  Register #(.width(5)) leftYreg (.D(multiplexer_6_out), .Q(leftYout), .clk(takt));  // open: en, clr
  Multiplexer #(.width(2)) multiplexer_8 (
    .in0(2'b01), .in1(multiplexer_7_out), .out(VrightBat), .sel(or_8_out));  // open: en
  or or_8 (or_8_out, comparator_1_eq, comparator_1_lt);
  and and_4 (LBcontact, xor_3_out, inrange_1_bus_0);
  and and_5 (RBcontact, xor_4_out, inrange_2_bus_0);
  Random #(.width(3)) random_1 (.clk(takt), .next(reset_t), .out(random_1_out));  // open: clr
  assign bit_extender_10_out = {{3{VrightBat[1]}}, VrightBat};  // Bit_Extender bit_extender_10
  or or_9 (Bcontact, LBcontact, RBcontact);
  mcon mcon_3 (.Vy(bit_extender_10_out), .Y(rightYout), .bus_0(gg));
  Comparator #(.width(3)) comparator_2 (.a(random_1_out), .b(3'b000), .eq(comparator_2_eq));  // open: gt, lt
  or or_10 (or_10_out, comparator_2_eq, comparator_3_eq);
  Comparator #(.width(3)) comparator_3 (.a(random_1_out), .b(3'b100), .eq(comparator_3_eq));  // open: gt, lt
  Adder #(.width(3)) adder_13 (.a(random_1_out), .b(3'b111), .out(adder_13_out));  // open: cin, cout
  Multiplexer #(.width(3)) multiplexer_9 (
    .in0(random_1_out), .in1(adder_13_out), .out(multiplexer_9_out), .sel(or_10_out));  // open: en
  or or_11 (or_11_out, yrefl, Bcontact);
  assign bit_extender_11_out = {{1{1'b0}}, random_2_out};  // Bit_Extender bit_extender_11
  Random #(.width(2)) random_2 (.clk(takt), .next(reset_t), .out(random_2_out));  // open: clr
  reflect reflect_1 (.in_1(vy), .out_2(reflect_1_out_2));
  Multiplexer #(.width(3)) multiplexer_10 (
    .in0(reflect_1_out_2), .in1(multiplexer_9_out), .out(multiplexer_10_out), .sel(reset_t));  // open: en
  Random #(.width(1)) random_3 (.clk(takt), .next(or_11_out), .out(random_3_out));  // open: clr
  reflect reflect_2 (.in_1(vx), .out_2(reflect_2_out_2));
  Multiplexer #(.width(3)) multiplexer_11 (
    .in0(reflect_2_out_2), .in1(adder_17_out), .out(multiplexer_11_out), .sel(reset_t));  // open: en
  Adder #(.width(3)) adder_14 (.a(multiplexer_10_out), .b(multiplexer_12_out), .out(adder_14_out));  // open: cin, cout
  Multiplexer #(.width(3)) multiplexer_12 (
    .in0(3'b001), .in1(3'b111), .out(multiplexer_12_out), .sel(random_3_out));  // open: en
  Adder #(.width(3)) adder_15 (.a(multiplexer_11_out), .b(multiplexer_12_out), .out(adder_15_out));  // open: cin, cout
  Comparator #(.width(3)) comparator_4 (.a(bit_extender_11_out), .b(3'b000), .eq(comparator_4_eq));  // open: gt, lt
  Adder #(.width(3)) adder_16 (.a(bit_extender_11_out), .b(3'b001), .out(adder_16_out));  // open: cin, cout
  Comparator #(.width(3)) comparator_5 (.a(adder_14_out), .b(3'b000), .eq(comparator_5_eq));  // open: gt, lt
  Comparator #(.width(3)) comparator_6 (.a(adder_14_out), .b(3'b100), .eq(comparator_6_eq));  // open: gt, lt
  Comparator #(.width(3)) comparator_7 (.a(adder_15_out), .b(3'b000), .eq(comparator_7_eq));  // open: gt, lt
  Comparator #(.width(3)) comparator_8 (.a(adder_15_out), .b(3'b100), .eq(comparator_8_eq));  // open: gt, lt
  Multiplexer #(.width(3)) multiplexer_13 (
    .in0(bit_extender_11_out), .in1(adder_16_out), .out(multiplexer_13_out), .sel(comparator_4_eq));  // open: en
  or or_12 (or_12_out, comparator_5_eq, comparator_6_eq);
  Multiplexer #(.width(3)) multiplexer_14 (
    .in0(multiplexer_11_out), .in1(adder_15_out), .out(xx), .sel(and_7_out));  // open: en
  or or_13 (or_13_out, comparator_7_eq, comparator_8_eq);
  assign not_5_out = ~multiplexer_13_out;  // NOT_Gate not_5, 3 bits wide
  not not_6 (not_6_out, or_12_out);
  and and_6 (and_6_out, not_6_out, yrefl);
  not not_7 (not_7_out, or_13_out);
  and and_7 (and_7_out, not_7_out, Bcontact);
  Adder #(.width(3)) adder_17 (.a(not_5_out), .b(3'b001), .out(adder_17_out));  // open: cin, cout
  Multiplexer #(.width(3)) multiplexer_15 (
    .in0(multiplexer_10_out), .in1(adder_14_out), .out(yy), .sel(and_6_out));  // open: en

  assign zero = {5{1'b0}};

  // Other names for the same wires on the sheet: r = reset; xreg[7:0] = xball; yreg[7:0] = yball
endmodule

// Video chips
module video8 (
  input  [4:0] ballX,
  input  [4:0] ballY,
  input  [4:0] leftbatY,
  input  [4:0] rightbatY,
  input  [4:0] chipID,
  output [31:0] ot1,
  output [31:0] ot2,
  output [31:0] ot3,
  output [31:0] ot4,
  output [31:0] ot5,
  output [31:0] ot6,
  output [31:0] ot7,
  output [31:0] ot8,
  output [4:0] ballX_2,
  output [4:0] ballY_2,
  output [4:0] leftbatY_2,
  output [4:0] rightbatY_2,
  output [4:0] chipID_2
);

  wire [4:0] video_1_ballx_2, video_1_bally_2, video_1_chipid_2, video_1_leftbaty_2, video_1_rightbaty_2,
       video_2_ballx_2, video_2_bally_2, video_2_chipid_2, video_2_leftbaty_2, video_2_rightbaty_2,
       video_3_ballx_2, video_3_bally_2, video_3_chipid_2, video_3_leftbaty_2, video_3_rightbaty_2,
       video_4_ballx_2, video_4_bally_2, video_4_chipid_2, video_4_leftbaty_2, video_4_rightbaty_2,
       video_5_ballx_2, video_5_bally_2, video_5_chipid_2, video_5_leftbaty_2, video_5_rightbaty_2,
       video_6_ballx_2, video_6_bally_2, video_6_chipid_2, video_6_leftbaty_2, video_6_rightbaty_2,
       video_7_ballx_2, video_7_bally_2, video_7_chipid_2, video_7_leftbaty_2, video_7_rightbaty_2;

  video video_1 (
    .ballX(video_2_ballx_2), .ballY(video_2_bally_2), .leftbatY(video_2_leftbaty_2),
    .rightbatY(video_2_rightbaty_2), .chipID(video_2_chipid_2), .ot(ot2), .ballX_2(video_1_ballx_2),
    .ballY_2(video_1_bally_2), .leftbatY_2(video_1_leftbaty_2), .rightbatY_2(video_1_rightbaty_2),
    .chipID_2(video_1_chipid_2));
  video video_2 (
    .ballX(ballX), .ballY(ballY), .leftbatY(leftbatY), .rightbatY(rightbatY), .chipID(chipID), .ot(ot1),
    .ballX_2(video_2_ballx_2), .ballY_2(video_2_bally_2), .leftbatY_2(video_2_leftbaty_2),
    .rightbatY_2(video_2_rightbaty_2), .chipID_2(video_2_chipid_2));
  video video_3 (
    .ballX(video_4_ballx_2), .ballY(video_4_bally_2), .leftbatY(video_4_leftbaty_2),
    .rightbatY(video_4_rightbaty_2), .chipID(video_4_chipid_2), .ot(ot4), .ballX_2(video_3_ballx_2),
    .ballY_2(video_3_bally_2), .leftbatY_2(video_3_leftbaty_2), .rightbatY_2(video_3_rightbaty_2),
    .chipID_2(video_3_chipid_2));
  video video_4 (
    .ballX(video_1_ballx_2), .ballY(video_1_bally_2), .leftbatY(video_1_leftbaty_2),
    .rightbatY(video_1_rightbaty_2), .chipID(video_1_chipid_2), .ot(ot3), .ballX_2(video_4_ballx_2),
    .ballY_2(video_4_bally_2), .leftbatY_2(video_4_leftbaty_2), .rightbatY_2(video_4_rightbaty_2),
    .chipID_2(video_4_chipid_2));
  video video_5 (
    .ballX(video_3_ballx_2), .ballY(video_3_bally_2), .leftbatY(video_3_leftbaty_2),
    .rightbatY(video_3_rightbaty_2), .chipID(video_3_chipid_2), .ot(ot5), .ballX_2(video_5_ballx_2),
    .ballY_2(video_5_bally_2), .leftbatY_2(video_5_leftbaty_2), .rightbatY_2(video_5_rightbaty_2),
    .chipID_2(video_5_chipid_2));
  video video_6 (
    .ballX(video_7_ballx_2), .ballY(video_7_bally_2), .leftbatY(video_7_leftbaty_2),
    .rightbatY(video_7_rightbaty_2), .chipID(video_7_chipid_2), .ot(ot7), .ballX_2(video_6_ballx_2),
    .ballY_2(video_6_bally_2), .leftbatY_2(video_6_leftbaty_2), .rightbatY_2(video_6_rightbaty_2),
    .chipID_2(video_6_chipid_2));
  video video_7 (
    .ballX(video_5_ballx_2), .ballY(video_5_bally_2), .leftbatY(video_5_leftbaty_2),
    .rightbatY(video_5_rightbaty_2), .chipID(video_5_chipid_2), .ot(ot6), .ballX_2(video_7_ballx_2),
    .ballY_2(video_7_bally_2), .leftbatY_2(video_7_leftbaty_2), .rightbatY_2(video_7_rightbaty_2),
    .chipID_2(video_7_chipid_2));
  video video_8 (
    .ballX(video_6_ballx_2), .ballY(video_6_bally_2), .leftbatY(video_6_leftbaty_2),
    .rightbatY(video_6_rightbaty_2), .chipID(video_6_chipid_2), .ot(ot8), .ballX_2(ballX_2),
    .ballY_2(ballY_2), .leftbatY_2(leftbatY_2), .rightbatY_2(rightbatY_2), .chipID_2(chipID_2));
endmodule

module mcon (
  input  [4:0] Vy,
  input  [4:0] Y,
  output [4:0] bus_0
);

  wire adder_2_cout, adder_3_cout, and_1_out, and_2_out, bit_extender_1_out, not_1_out, not_2_out, or_1_out;
  wire [4:0] adder_1_out, NY, shifter_1_out;

  Adder #(.width(5)) adder_1 (.a(Y), .b(5'b00010), .out(adder_1_out));  // open: cin, cout
  Adder #(.width(5)) adder_2 (.a(Vy), .b(Y), .out(NY), .cout(adder_2_cout));  // open: cin
  Bit_Extender #(.in_width(5), .out_width(1)) bit_extender_1 (.in(shifter_1_out), .out(bit_extender_1_out));
  Shifter #(.width(5), .shift("lr")) shifter_1 (.in(Vy), .\dist (3'b100), .out(shifter_1_out));
  Adder #(.width(5)) adder_3 (.a(Vy), .b(adder_1_out), .cout(adder_3_cout));  // open: out, cin
  not not_1 (not_1_out, bit_extender_1_out);
  not not_2 (not_2_out, adder_2_cout);
  and and_1 (and_1_out, not_1_out, adder_3_cout);
  and and_2 (and_2_out, bit_extender_1_out, not_2_out);
  or or_1 (or_1_out, and_1_out, and_2_out);
  Multiplexer #(.width(5)) multiplexer_1 (.in0(NY), .in1(Y), .out(bus_0), .sel(or_1_out));  // open: en
endmodule

// CDM8
module rob (
  input  [7:0] vxy,
  input  [7:0] xball,
  input  [7:0] yball,
  input  [7:0] lvl,
  output [4:0] out_5
);

  wire and_2_out, and_3_out, and_4_out, and_5_out, cdm_8_mark5_1_p1, cdm_8_mark5_1_p2, cdm_8_mark5_1_p4,
       cdm_8_mark5_1_p5, cdm_8_mark5_1_p6, cdm_8_mark5_1_p7, cdm_8_mark5_1_p8, cdm_8_mark5_1_p9,
       cdm_8_mark5_1_p10, clk, decoder_1_out0, decoder_1_out1, decoder_2_out0, decoder_2_out1,
       decoder_3_out0, decoder_3_out1, IO_3_2_out, IO_3_3_out, IO_3_4_out, IO_3_5_out, IO_3_out, IOsel,
       not_1_out, READwrite;
  wire [3:0] IOaddr;
  wire [7:0] cdm_8_mark5_1_p13, cdm_8_mark5_1_p14, IOdat, register_1_q, register_2_q;
  wire [7:4] cdm_8_mark5_1_p12;

  Clock clock_1 (.out(clk));
  // Probe on cdm_8_mark5_1_p1
  assign IOdat = and_2_out ? vxy : 8'bz;  // Controlled_Buffer controlled_buffer_1
  // Probe on cdm_8_mark5_1_p5
  // Probe on cdm_8_mark5_1_p4
  // Probe on cdm_8_mark5_1_p2
  // Probe on cdm_8_mark5_1_p6
  // Probe on cdm_8_mark5_1_p7
  and IO_3 (IO_3_out, IOsel, IOaddr[0], ~IOaddr[1], ~IOaddr[2], ~IOaddr[3]);  // AND_Gate
  and and_1 (IOsel, cdm_8_mark5_1_p12[4], cdm_8_mark5_1_p12[5], cdm_8_mark5_1_p12[6], cdm_8_mark5_1_p12[7], decoder_1_out1);
  // Probe on cdm_8_mark5_1_p8
  Decoder #(.disabled(0)) decoder_1 (
    .out0(decoder_1_out0), .out1(decoder_1_out1), .sel(cdm_8_mark5_1_p9), .en(cdm_8_mark5_1_p10));
  // CdM_8_mark5 cdm_8_mark5_1: pin names not known; wires that end beside it: cdm_8_mark5_1_p1, cdm_8_mark5_1_p2, clk, cdm_8_mark5_1_p4, cdm_8_mark5_1_p5, cdm_8_mark5_1_p6, cdm_8_mark5_1_p7, cdm_8_mark5_1_p8, cdm_8_mark5_1_p9, cdm_8_mark5_1_p10, READwrite, {cdm_8_mark5_1_p12, IOaddr}, cdm_8_mark5_1_p13, cdm_8_mark5_1_p14
  not not_1 (not_1_out, READwrite);
  assign cdm_8_mark5_1_p14 = READwrite ? IOdat : 8'bz;  // Controlled_Buffer controlled_buffer_2
  and and_2 (and_2_out, READwrite, IO_3_out);
  assign IOdat = and_4_out ? xball : 8'bz;  // Controlled_Buffer controlled_buffer_3
  assign IOdat = not_1_out ? cdm_8_mark5_1_p13 : 8'bz;  // Controlled_Buffer controlled_buffer_4
  // Probe on {cdm_8_mark5_1_p12, IOaddr}
  and and_3 (and_3_out, decoder_1_out1, ~IOsel);  // AND_Gate
  and and_4 (and_4_out, READwrite, IO_3_2_out);
  and IO_3_2 (IO_3_2_out, IOsel, ~IOaddr[0], IOaddr[1], ~IOaddr[2], ~IOaddr[3]);  // AND_Gate
  assign IOdat = decoder_2_out1 ? yball : 8'bz;  // Controlled_Buffer controlled_buffer_5
  // Probe on IOdat
  RAM ram_1 (
    .addr({cdm_8_mark5_1_p12, IOaddr}), .data(IOdat), .sel(and_3_out), .clk(clk), .ld(READwrite));  // open: clr
  ROM rom_1 (.addr({cdm_8_mark5_1_p12, IOaddr}), .data(IOdat), .sel(decoder_1_out0));
  and IO_3_3 (IO_3_3_out, IOsel, IOaddr[0], IOaddr[1], ~IOaddr[2], ~IOaddr[3]);  // AND_Gate
  Decoder #(.disabled(0)) decoder_2 (.out0(decoder_2_out0), .out1(decoder_2_out1), .sel(READwrite), .en(IO_3_3_out));
  Bit_Extender #(.out_width(5)) bit_extender_1 (.in(register_1_q), .out(out_5));
  Register #(.trigger("falling")) register_1 (
    .D(IOdat), .en(decoder_2_out0), .Q(register_1_q), .clk(clk));  // open: clr
  assign IOdat = and_5_out ? lvl : 8'bz;  // Controlled_Buffer controlled_buffer_6
  and and_5 (and_5_out, READwrite, IO_3_4_out);
  and IO_3_4 (IO_3_4_out, IOsel, ~IOaddr[0], ~IOaddr[1], IOaddr[2], ~IOaddr[3]);  // AND_Gate
  assign IOdat = decoder_3_out1 ? register_2_q : 8'bz;  // Controlled_Buffer controlled_buffer_7
  Decoder #(.disabled(0)) decoder_3 (.out0(decoder_3_out0), .out1(decoder_3_out1), .sel(READwrite), .en(IO_3_5_out));
  and IO_3_5 (IO_3_5_out, IOsel, IOaddr[0], ~IOaddr[1], IOaddr[2], ~IOaddr[3]);  // AND_Gate
  Register #(.trigger("falling")) register_2 (
    .D(IOdat), .en(decoder_3_out0), .Q(register_2_q), .clk(clk));  // open: clr

  // Notes on the sheet:
  //   contents of rom_1 (hex, n*v repeats v):
  //   d0 f1 b0 d1 f2 b5 d2 f3 ba d3 f5 ae d3 e0 3d d3 f4 bf f e1 18 99 ee 28 d3 7 43 d2 2 7e e1 21 99 d2 3
  //   7e e1 28 99 99 d3 f5 bf e d3 38 4c 98 98 98 d3 4 73 e5 4d d3 2 73 e1 3d 95 d3 3 73 e1 45 7 95 1d 19
  //   e3 4b d3 ff 3d ee 67 d3 ff 3e d3 6 73 e1 56 95 d3 5 73 e1 5e 7 95 1d 19 e3 64 d3 ff 3d d3 ff 3d 99
  //   99 99 d3 f3 ad ee
endmodule

// score
module sc (
  input  [7:0] in_1,
  output [3:0] out_2,
  output [3:0] out_3
);

  wire [7:0] divider_1_rem, divider_2_out, divider_2_rem;

  Divider divider_1 (.a(in_1), .b(8'h64), .rem(divider_1_rem));  // open: out, upper
  Divider divider_2 (.a(divider_1_rem), .b(8'ha), .out(divider_2_out), .rem(divider_2_rem));  // open: upper
  Bit_Extender #(.out_width(4)) bit_extender_1 (.in(divider_2_out), .out(out_2));
  Bit_Extender #(.out_width(4)) bit_extender_2 (.in(divider_2_rem), .out(out_3));
endmodule

module lvl (
  input  in_1,
  input  in_2,
  output out_3,
  output [7:0] out_4
);

  wire clock_1_out, controlled_buffer_1_out, not_1_out, or_1_out;

  assign controlled_buffer_1_out = in_1 ? in_1 : 1'bz;  // Controlled_Buffer controlled_buffer_1
  assign controlled_buffer_1_out = in_2 ? not_1_out : 1'bz;  // Controlled_Buffer controlled_buffer_2
  not not_1 (not_1_out, in_2);
  or or_1 (or_1_out, in_1, in_2);
  Register #(.width(1)) register_1 (
    .D(controlled_buffer_1_out), .en(or_1_out), .Q(out_3), .clk(clock_1_out));  // open: clr
  Clock clock_1 (.out(clock_1_out));
  assign out_4 = {{7{1'b0}}, out_3};  // Bit_Extender bit_extender_1
endmodule
